// Logisim project 8Bit_MIPS_Processor.circ as structural Verilog: 6 circuits, main circuit main
module main (
  input  in_1
);

  wire clock_1_out, control_unit_1_memread, control_unit_1_memtoreg, control_unit_1_memwrite,
       control_unit_1_regdst, control_unit_1_regwrite, control_unit_1_sub;
  wire [1:0] multiplexer_1_out, rom_1_data_2;
  wire [5:0] rom_1_data;
  wire [7:0] ALU_out, multiplexer_2_out, pc_1_out, ram_1_data, registers_1_readdata1, registers_1_readdata2;

  PC pc_1 (.Clock(clock_1_out), .Reset(in_1), .Out(pc_1_out));
  Clock clock_1 (.out(clock_1_out));
  ROM rom_1 (.addr(pc_1_out), .data({rom_1_data_2, rom_1_data}));  // open: sel
  Control_Unit control_unit_1 (
    .Op(rom_1_data_2), .RegDst(control_unit_1_regdst), .RegWrite(control_unit_1_regwrite),
    .Sub(control_unit_1_sub), .MemRead(control_unit_1_memread), .MemWrite(control_unit_1_memwrite),
    .memtoReg(control_unit_1_memtoreg));
  Multiplexer #(.width(2), .enable("false")) multiplexer_1 (
    .in0(rom_1_data[5:4]), .in1(rom_1_data[1:0]), .out(multiplexer_1_out), .sel(control_unit_1_regdst));
  Registers registers_1 (
    .WriteData(multiplexer_2_out), .WriteReg(rom_1_data[5:4]), .RegWrite(control_unit_1_regwrite),
    .Clock(clock_1_out), .ReadData1(registers_1_readdata1), .ReadReg1(rom_1_data[3:2]),
    .ReadData2(registers_1_readdata2), .ReadReg2(multiplexer_1_out));
  Multiplexer #(.width(8)) multiplexer_2 (
    .in0(ALU_out), .in1(ram_1_data), .out(multiplexer_2_out), .sel(control_unit_1_memtoreg));  // open: en
  ALU ALU (
    .In_A(registers_1_readdata1), .In_B(registers_1_readdata2), .Control_bit(control_unit_1_sub),
    .Out(ALU_out));  // open: Zero
  RAM #(.bus("separate")) ram_1 (
    .addr({4'b0000, rom_1_data[3:0]}), .din(registers_1_readdata2), .data(ram_1_data),
    .str(control_unit_1_memwrite), .clk(clock_1_out), .ld(control_unit_1_memread));  // open: sel, clr

  // Notes on the sheet:
  //   PC
  //   Instruction Mem
  //   contents of rom_1 (hex, n*v repeats v):
  //   0 11 22 81 82 13 24 35 96 97 e4 66
  //   Register FIle
  //   Data Mem
endmodule

module ALU (
  input  Control_bit,
  input  [7:0] In_A,
  input  [7:0] In_B,
  output [7:0] Out,
  output Zero
);

  wire or_1_out;
  wire [7:0] xor_1_out;

  assign xor_1_out = {8{Control_bit}} ^ In_B;  // XOR_Gate xor_1, 8 bits wide
  Adder adder_1 (.a(In_A), .b(xor_1_out), .out(Out), .cin(Control_bit));  // open: cout
  or or_1 (or_1_out, Out[0], Out[1], Out[2], Out[3], Out[4], Out[5], Out[6], Out[7]);
  not not_1 (Zero, or_1_out);
endmodule

module Registers (
  input  [7:0] WriteData,
  input  [1:0] WriteReg,
  input  [1:0] ReadReg1,
  input  [1:0] ReadReg2,
  input  RegWrite,
  input  Clock,
  output [7:0] ReadData1,
  output [7:0] ReadData2
);

  wire and_1_out, and_2_out, and_3_out, and_4_out, decoder_1_out0, decoder_1_out1, decoder_1_out2,
       decoder_1_out3;
  wire [7:0] multiplexer_1_out, multiplexer_2_out, multiplexer_3_out, multiplexer_4_out, register_1_q,
       register_2_q, register_3_q, register_4_q;

  Decoder #(.select(2), .enable("false")) decoder_1 (
    .out0(decoder_1_out0), .out1(decoder_1_out1), .out2(decoder_1_out2), .out3(decoder_1_out3), .sel(WriteReg));
  and and_1 (and_1_out, decoder_1_out0, RegWrite);
  and and_2 (and_2_out, decoder_1_out1, RegWrite);
  and and_3 (and_3_out, decoder_1_out2, RegWrite);
  and and_4 (and_4_out, decoder_1_out3, RegWrite);
  Multiplexer #(.width(8), .enable("false")) multiplexer_1 (
    .in0(register_1_q), .in1(WriteData), .out(multiplexer_1_out), .sel(and_1_out));
  Multiplexer #(.width(8), .enable("false")) multiplexer_2 (
    .in0(register_2_q), .in1(WriteData), .out(multiplexer_2_out), .sel(and_2_out));
  Multiplexer #(.width(8), .enable("false")) multiplexer_3 (
    .in0(register_3_q), .in1(WriteData), .out(multiplexer_3_out), .sel(and_3_out));
  Multiplexer #(.width(8), .enable("false")) multiplexer_4 (
    .in0(register_4_q), .in1(WriteData), .out(multiplexer_4_out), .sel(and_4_out));
  Register register_1 (.D(multiplexer_1_out), .Q(register_1_q), .clk(Clock));  // open: en, clr
  Register register_2 (.D(multiplexer_2_out), .Q(register_2_q), .clk(Clock));  // open: en, clr
  Register register_3 (.D(multiplexer_3_out), .Q(register_3_q), .clk(Clock));  // open: en, clr
  Register register_4 (.D(multiplexer_4_out), .Q(register_4_q), .clk(Clock));  // open: en, clr
  Multiplexer #(.select(2), .width(8), .enable("false")) multiplexer_5 (
    .in0(register_1_q), .in1(register_2_q), .in2(register_3_q), .in3(register_4_q), .out(ReadData1),
    .sel(ReadReg1));
  Multiplexer #(.select(2), .width(8), .enable("false")) multiplexer_6 (
    .in0(register_1_q), .in1(register_2_q), .in2(register_3_q), .in3(register_4_q), .out(ReadData2),
    .sel(ReadReg2));

  // Notes on the sheet:
  //   Register File 8x8-bits
endmodule

// Control
module Control_Unit (
  input  [1:0] Op,
  output RegDst,
  output RegWrite,
  output Sub,
  output MemRead,
  output MemWrite,
  output memtoReg
);

  wire not_1_out, not_2_out;

  not not_1 (not_1_out, Op[0]);
  not not_2 (not_2_out, Op[1]);
  or or_1 (RegWrite, Op[1], not_1_out);
  and and_1 (Sub, Op[1], Op[0]);
  and and_2 (MemRead, not_2_out, not_1_out);
  and and_3 (MemWrite, not_2_out, Op[0]);

  assign memtoReg = MemRead;
  assign RegDst = Op[1];
endmodule

module PC (
  input  Clock,
  input  Reset,
  output [7:0] Out
);

  wire [7:0] adder_1_out;

  Adder adder_1 (.a(8'h1), .b(Out), .out(adder_1_out));  // open: cin, cout
  Register register_1 (.D(adder_1_out), .Q(Out), .clk(Clock), .clr(Reset));  // open: en
endmodule

module testing_circuit (
  input  in_1,
  input  in_2,
  output [7:0] Mux_Out,
  output [7:0] Mem_Out,
  output [7:0] Alu_Out,
  output [7:0] ReadData1,
  output [1:0] out_7,
  output [1:0] out_8,
  output [7:0] out_9,
  output [1:0] readreg1,
  output [7:0] out_11,
  output [1:0] readreg2
);

  wire and_1_out, and_2_out, and_3_out, and_4_out, clock_1_out, control_unit_1_memread,
       control_unit_1_memtoreg, control_unit_1_memwrite, control_unit_1_regdst, control_unit_1_regwrite,
       control_unit_1_sub, decoder_1_out0, decoder_1_out1, decoder_1_out2, decoder_1_out3;
  wire [7:0] multiplexer_1_out, multiplexer_2_out, multiplexer_3_out, multiplexer_4_out, pc_1_out,
       register_1_q, register_2_q, register_3_q, register_4_q;

  PC pc_1 (.Clock(clock_1_out), .Reset(in_1), .Out(pc_1_out));
  Clock clock_1 (.out(clock_1_out));
  Control_Unit control_unit_1 (
    .Op(out_7), .RegDst(control_unit_1_regdst), .RegWrite(control_unit_1_regwrite), .Sub(control_unit_1_sub),
    .MemRead(control_unit_1_memread), .MemWrite(control_unit_1_memwrite), .memtoReg(control_unit_1_memtoreg));
  ROM rom_1 (.addr(pc_1_out), .data({out_7, out_8, out_11[3:0]}));  // open: sel
  Decoder #(.select(2), .enable("false")) decoder_1 (
    .out0(decoder_1_out0), .out1(decoder_1_out1), .out2(decoder_1_out2), .out3(decoder_1_out3), .sel(out_8));
  and and_1 (and_1_out, decoder_1_out0, control_unit_1_regwrite);
  and and_2 (and_2_out, decoder_1_out1, control_unit_1_regwrite);
  and and_3 (and_3_out, decoder_1_out2, control_unit_1_regwrite);
  and and_4 (and_4_out, decoder_1_out3, control_unit_1_regwrite);
  Multiplexer #(.width(8), .enable("false")) multiplexer_1 (
    .in0(register_1_q), .in1(Mux_Out), .out(multiplexer_1_out), .sel(and_1_out));
  Multiplexer #(.width(8), .enable("false")) multiplexer_2 (
    .in0(register_2_q), .in1(Mux_Out), .out(multiplexer_2_out), .sel(and_2_out));
  Multiplexer #(.width(8), .enable("false")) multiplexer_3 (
    .in0(register_3_q), .in1(Mux_Out), .out(multiplexer_3_out), .sel(and_3_out));
  Multiplexer #(.width(8), .enable("false")) multiplexer_4 (
    .in0(register_4_q), .in1(Mux_Out), .out(multiplexer_4_out), .sel(and_4_out));
  Register register_1 (.D(multiplexer_1_out), .Q(register_1_q), .clk(clock_1_out), .clr(in_2));  // open: en
  Register register_2 (.D(multiplexer_2_out), .Q(register_2_q), .clk(clock_1_out), .clr(in_2));  // open: en
  Register register_3 (.D(multiplexer_3_out), .Q(register_3_q), .clk(clock_1_out), .clr(in_2));  // open: en
  Register register_4 (.D(multiplexer_4_out), .Q(register_4_q), .clk(clock_1_out), .clr(in_2));  // open: en
  Multiplexer #(.select(2), .width(8), .enable("false")) multiplexer_5 (
    .in0(register_1_q), .in1(register_2_q), .in2(register_3_q), .in3(register_4_q), .out(ReadData1),
    .sel(out_11[3:2]));
  Multiplexer #(.select(2), .width(8), .enable("false")) multiplexer_6 (
    .in0(register_1_q), .in1(register_2_q), .in2(register_3_q), .in3(register_4_q), .out(out_9),
    .sel(readreg2));
  Multiplexer #(.width(2), .enable("false")) multiplexer_7 (
    .in0(out_8), .in1(out_11[1:0]), .out(readreg2), .sel(control_unit_1_regdst));
  Multiplexer #(.width(8)) multiplexer_8 (
    .in0(Alu_Out), .in1(Mem_Out), .out(Mux_Out), .sel(control_unit_1_memtoreg));  // open: en
  ALU alu_1 (.In_A(ReadData1), .In_B(out_9), .Control_bit(control_unit_1_sub), .Out(Alu_Out));  // open: Zero
  RAM #(.bus("separate")) ram_1 (
    .addr({4'b0000, out_11[3:0]}), .din(out_9), .data(Mem_Out), .str(control_unit_1_memwrite),
    .clk(clock_1_out), .ld(control_unit_1_memread));  // open: sel, clr

  assign out_11[7:4] = 4'b0000;
  assign readreg1 = out_11[3:2];

  // Notes on the sheet:
  //   contents of rom_1 (hex, n*v repeats v):
  //   0 11 22 81 82 13 24 35 96 97 e4 66
  //   REGDST
endmodule
