// Logisim project 8bitAdder.circ as structural Verilog: 1 circuit, main circuit main
module main (
  input  Control_bit,
  input  [7:0] In_A,
  input  [7:0] In_B,
  output Zero
);

  wire or_1_out;
  wire [7:0] adder_1_out, xor_1_out;

  assign xor_1_out = {8{Control_bit}} ^ In_B;  // XOR_Gate xor_1, 8 bits wide
  Adder adder_1 (.a(In_A), .b(xor_1_out), .out(adder_1_out), .cin(Control_bit));  // open: cout
  Hex_Digit_Display hex_digit_display_1 (.value(adder_1_out[7:4]));  // open: dp
  Hex_Digit_Display hex_digit_display_2 (.value(adder_1_out[3:0]));  // open: dp
  or or_1 (or_1_out, adder_1_out[0], adder_1_out[1], adder_1_out[2], adder_1_out[3], adder_1_out[4], adder_1_out[5], adder_1_out[6], adder_1_out[7]);
  not not_1 (Zero, or_1_out);
endmodule
